# Fritzing sketch lcd-meu-system-schematic-diagram (saved by Fritzing 0.9.2b)

parts:
  LCD2 = LCD screen
  LCM1602_IIC2 = LCM1602 IIC [part_number="LCM1602 IIC" chip_label="LCM1602 IIC" package="DIP (Dual Inline) [THT]"]
  Componente1 = Arduino Uno (Rev3) - ICSP
  R1 = Resistor [tolerance=±5% resistance=10k package="0805 [SMD]"]
  S1 = Momentary Switch [package=ksa_sealed_tac_switch]

nets:
  VSS: LCD2.VSS, LCM1602_IIC2.VSS
  VDD: LCD2.VDD, LCM1602_IIC2.VDD
  N1: LCD2.V0, LCM1602_IIC2.V0
  N2: LCD2.RS, LCM1602_IIC2.RS
  N3: LCD2.R/W, LCM1602_IIC2.RW
  N4: LCD2.E, LCM1602_IIC2.E
  N5: LCD2.DB0, LCM1602_IIC2.D0
  N6: LCD2.DB1, LCM1602_IIC2.D1
  N7: LCD2.DB2, LCM1602_IIC2.D2
  N8: LCD2.DB3, LCM1602_IIC2.D3
  N9: LCD2.DB4, LCM1602_IIC2.D4
  N10: LCD2.DB5, LCM1602_IIC2.D5
  N11: LCD2.DB6, LCM1602_IIC2.D6
  N12: LCD2.DB7, LCM1602_IIC2.D7
  N13: LCD2.LED+, LCM1602_IIC2.A
  N14: LCD2.LED-, LCM1602_IIC2.K
  GND: LCM1602_IIC2.GND, Componente1.GND, S1.4
  VCC: LCM1602_IIC2.VCC, Componente1.5V, R1.Pin_1
  N15: LCM1602_IIC2.SDA, Componente1.A4/SDA
  N16: LCM1602_IIC2.SCL, Componente1.A5/SCL
  N17: LCM1602_IIC2.LED_A, LCM1602_IIC2.LED_B
  N18: Componente1.D4, R1.Pin_0, S1.2

custom parts:
  LCM1602 IIC: I2C-Module to use a 1602 or 2004 LCD on with the wire.h libory Serial LCD Modul
